// Logisim project main.circ as structural Verilog: 4 circuits, main circuit main
module main (
);

  wire clock_1_out;
  wire [31:0] fetch_sub_1_out, if_id_pipeline_register_1_instruction_2, if_id_pipeline_register_1_pc_4_2,
       mipsprogramrom_1_p2;

  Clock clock_1 (.out(clock_1_out));
  Fetch_Sub fetch_sub_1 (.Clock(clock_1_out), .Out(fetch_sub_1_out));
  // MIPSProgramROM mipsprogramrom_1: pin names not known; wires that end beside it: fetch_sub_1_out, mipsprogramrom_1_p2
  IF_ID_Pipeline_Register if_id_pipeline_register_1 (
    .PC_4(fetch_sub_1_out), .Instruction(mipsprogramrom_1_p2), .Clock(clock_1_out),
    .PC_4_2(if_id_pipeline_register_1_pc_4_2), .Instruction_2(if_id_pipeline_register_1_instruction_2));
endmodule

module PC_Inc (
  input  [31:0] Input,
  output [31:0] Output
);

  // Incrementer incrementer_1: pin names not known; wires that end beside it: Input[31:2], Output[31:2]

  assign Output[1:0] = Input[1:0];
endmodule

// PC+4
module Fetch_Sub (
  input  Clock,
  output [31:0] Out
);

  wire [31:0] pc_inc_1_output;

  Register #(.width(32)) register_1 (.D(pc_inc_1_output), .Q(Out), .clk(Clock));  // open: en, clr
  PC_Inc pc_inc_1 (.Input(Out), .Output(pc_inc_1_output));
endmodule

// IF/ID
module IF_ID_Pipeline_Register (
  input  [31:0] PC_4,
  input  [31:0] Instruction,
  input  Clock,
  output [31:0] PC_4_2,
  output [31:0] Instruction_2
);

  Register #(.width(32)) u_PC_4 (.D(PC_4), .Q(PC_4_2), .clk(Clock));  // open: en, clr
  Register #(.width(32)) u_Instruction (.D(Instruction), .Q(Instruction_2), .clk(Clock));  // open: en, clr
endmodule
